# Fritzing sketch MPR121-Sketch (saved by Fritzing 0.9.3b)

parts:
  Arduino_Nano = Arduino Nano (Rev3.0)
  MPR121 = Adafruit MPR121

nets:
  GND: Arduino_Nano.GND, MPR121.GND
  N1: Arduino_Nano.D2, MPR121.IRQ
  N2: Arduino_Nano.A5, MPR121.SCL
  N3: Arduino_Nano.A4, MPR121.SDA
  3V3: Arduino_Nano.3V3, MPR121.3.3V

custom parts:
  Adafruit MPR121: Add lots of touch sensors to your next microcontroller project with this easy-to-use 12-channel capacitive touch sensor breakout board, starring the MPR121. This chip can handle up to 12 individual touch pads. The MPR121 has support for only I2C, which can be implemented with nearly any microcontroller. You can select one of 4 addresses with the ADDR pin, for a total of 48 capacitive touch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
